# Fritzing sketch theremino (saved by Fritzing 0.8.0b)
breadboards: 1

parts:
  Part1 = Arduino Uno (Rev3)
  Part2 = SRF05 Ultrasonic Rangefinder
  J1 = Piezo Speaker

nets:
  GND: Part1.GND, Part2.GND, J1.pin1
  N1: Part1.D9_PWM, J1.pin2
  N2: Part1.D2, Part2.Trig
  N3: Part1.D3_PWM, Part2.Echo
  5V: Part1.5V, Part2.VCC
